// Logisim project Processor.circ as structural Verilog: 35 circuits, main circuit main
module main (
  input  in_1,
  input  clear_bit,
  output out_3
);

  wire alu_1_regwrite_signal, clock_1_out, cpu_1_add, cpu_1_alu_signal, cpu_1_and, cpu_1_beq, cpu_1_bge,
       cpu_1_bgt, cpu_1_ble, cpu_1_blt, cpu_1_defaullt_offset_signal, cpu_1_imm_add, cpu_1_imm_and,
       cpu_1_imm_or, cpu_1_imm_signal, cpu_1_imm_xor, cpu_1_jump, cpu_1_jump_offset_signal, cpu_1_load,
       cpu_1_or, cpu_1_xor, or_1_out;
  wire [1:0] cpu_1_store, offset_selector_1_offset_selector;
  wire [3:0] alu_separator_1_dest, alu_separator_1_source_1, alu_separator_1_source_2,
       branch_separator_1_read_register_1, branch_separator_1_read_register_2, multiplexer_2_out,
       multiplexer_3_out, multiplexer_4_out, ram_separator_1_load_register;
  wire [5:0] branch_separator_1_branch_address;
  wire [9:0] address_stabiliser_1_output_address, branch_stabiliser_1_branch_offset,
       jump_parser_1_jump_offset, pc_1_current_address, ram_separator_1_memory_address;
  wire [13:0] cpu_1_process_data;
  wire [17:0] alu_1_alu_result, alu_separator_1__18_bit_output, multiplexer_1_out, multiplexer_5_out,
       n18_bit_register_1_read_data_1, n18_bit_register_1_read_data_2, ram_1_data, rom_1_data;

  Clock clock_1 (.out(clock_1_out));
  PC pc_1 (
    .clock(clock_1_out), .branch_offset(branch_stabiliser_1_branch_offset),
    .jump_offset(address_stabiliser_1_output_address), .address_signal(offset_selector_1_offset_selector),
    .reset_signal(in_1), .address_overflow(out_3), .current_address(pc_1_current_address));
  Multiplexer #(.width(18)) multiplexer_1 (
    .in0(alu_1_alu_result), .in1(ram_1_data), .out(multiplexer_1_out), .sel(cpu_1_load));  // open: en
  Multiplexer #(.width(4)) multiplexer_2 (
    .in0(alu_separator_1_dest), .in1(ram_separator_1_load_register), .out(multiplexer_2_out), .sel(cpu_1_load));  // open: en
  Multiplexer #(.select(2), .width(4)) multiplexer_3 (
    .in0(alu_separator_1_source_1), .in1(ram_separator_1_load_register),
    .in2(branch_separator_1_read_register_1), .out(multiplexer_3_out), .sel(cpu_1_store));  // open: in3, en
  Multiplexer #(.width(4)) multiplexer_4 (
    .in0(alu_separator_1_source_2), .in1(branch_separator_1_read_register_2), .out(multiplexer_4_out),
    .sel(cpu_1_store[1]));  // open: en
  _18_bit_register u_18_bit_register_1 (
    .read_register_1(multiplexer_3_out), .write_register(multiplexer_2_out),
    .read_register_2(multiplexer_4_out), .input_data(multiplexer_1_out),
    .read_data_1(n18_bit_register_1_read_data_1), .read_data_2(n18_bit_register_1_read_data_2),
    .regWrite(or_1_out), .Clock(clock_1_out), .reset_siignal(clear_bit));
  ROM #(.addrWidth(10), .dataWidth(18)) rom_1 (.addr(pc_1_current_address), .data(rom_1_data), .sel(1'b1));
  ALU_separator alu_separator_1 (
    ._14_bit_input(cpu_1_process_data), ._18_bit_output(alu_separator_1__18_bit_output),
    .Dest(alu_separator_1_dest), .Source_1(alu_separator_1_source_1), .Source_2(alu_separator_1_source_2));
  address_stabiliser address_stabiliser_1 (
    .output_address(address_stabiliser_1_output_address), .current_address(pc_1_current_address),
    .offset(jump_parser_1_jump_offset));  // open: overflow
  jump_parser jump_parser_1 (
    .jump_offset(jump_parser_1_jump_offset), .input_data(cpu_1_process_data), .jump_signal(cpu_1_jump));
  Multiplexer #(.width(18)) multiplexer_5 (
    .in0(n18_bit_register_1_read_data_2), .in1(alu_separator_1__18_bit_output), .out(multiplexer_5_out),
    .sel(cpu_1_imm_signal));  // open: en
  offset_selector offset_selector_1 (
    .jump(cpu_1_jump_offset_signal), .branch(cpu_1_store[1]), .\default (cpu_1_defaullt_offset_signal),
    .offset_selector(offset_selector_1_offset_selector));
  CPU cpu_1 (
    .assembly_code(rom_1_data), .process_data(cpu_1_process_data), .imm_signal(cpu_1_imm_signal),
    .alu_signal(cpu_1_alu_signal), .add(cpu_1_add), .\and (cpu_1_and), .\or (cpu_1_or), .\xor (cpu_1_xor),
    .imm_add(cpu_1_imm_add), .imm_and(cpu_1_imm_and), .imm_or(cpu_1_imm_or), .imm_xor(cpu_1_imm_xor),
    .jump(cpu_1_jump), .load(cpu_1_load), .store(cpu_1_store[0]), .beq(cpu_1_beq), .blt(cpu_1_blt),
    .bgt(cpu_1_bgt), .ble(cpu_1_ble), .bge(cpu_1_bge), .jump_offset_signal(cpu_1_jump_offset_signal),
    .branch_offset_signal(cpu_1_store[1]), .defaullt_offset_signal(cpu_1_defaullt_offset_signal));
  ram_separator ram_separator_1 (
    .process_data(cpu_1_process_data), .load_register(ram_separator_1_load_register),
    .memory_address(ram_separator_1_memory_address));
  or or_1 (or_1_out, cpu_1_load, alu_1_regwrite_signal);
  ALU alu_1 (
    .data_1(n18_bit_register_1_read_data_1), .data_2(multiplexer_5_out), .ALU_signal(cpu_1_alu_signal),
    .in_4(cpu_1_add), .in_5(cpu_1_imm_add), .and_signals(cpu_1_and), .in_7(cpu_1_imm_and),
    .or_signals(cpu_1_or), .in_9(cpu_1_imm_or), .xor_signals(cpu_1_xor), .in_11(cpu_1_imm_xor),
    .alu_result(alu_1_alu_result), .regWrite_signal(alu_1_regwrite_signal));  // open: overflow_bit
  branch_stabiliser branch_stabiliser_1 (
    .beq(cpu_1_beq), .blt(cpu_1_blt), .bgt(cpu_1_bgt), .ble(cpu_1_ble), .bge(cpu_1_bge),
    .register_1(n18_bit_register_1_read_data_1), .register_2(n18_bit_register_1_read_data_2),
    .offset(branch_separator_1_branch_address), .current_pc_address(pc_1_current_address),
    .branch_offset(branch_stabiliser_1_branch_offset));  // open: overflow
  branch_separator branch_separator_1 (
    .process_data(cpu_1_process_data), .branch_signal(cpu_1_store[1]),
    .read_register_1(branch_separator_1_read_register_1),
    .read_register_2(branch_separator_1_read_register_2), .branch_address(branch_separator_1_branch_address));
  RAM #(.addrWidth(10), .dataWidth(18), .bus("separate")) ram_1 (
    .addr(ram_separator_1_memory_address), .din(n18_bit_register_1_read_data_1), .data(ram_1_data),
    .str(cpu_1_store[0]), .sel(1'b1), .clk(clock_1_out), .ld(cpu_1_load));  // open: clr

  // Notes on the sheet:
  //   contents of rom_1 (hex, n*v repeats v):
  //   24000 24401 24802 24c03 25004 2c4fd
endmodule

module _1_bit_half_adder (
  input  in_1,
  input  in_2,
  output out_3,
  output out_4
);

  xor xor_1 (out_3, in_1, in_2);
  and and_1 (out_4, in_1, in_2);
endmodule

module _1_bit_full_adder (
  input  in_1,
  input  in_2,
  input  in_3,
  output out_4,
  output out_5
);

  wire n1_bit_half_adder_1_out_3, n1_bit_half_adder_1_out_4, n1_bit_half_adder_2_out_4;

  _1_bit_half_adder u_1_bit_half_adder_1 (
    .in_1(in_2), .in_2(in_3), .out_3(n1_bit_half_adder_1_out_3), .out_4(n1_bit_half_adder_1_out_4));
  _1_bit_half_adder u_1_bit_half_adder_2 (
    .in_1(in_1), .in_2(n1_bit_half_adder_1_out_3), .out_3(out_4), .out_4(n1_bit_half_adder_2_out_4));
  or or_1 (out_5, n1_bit_half_adder_2_out_4, n1_bit_half_adder_1_out_4);
endmodule

module _2_bit_adder (
  input  in_1,
  input  [1:0] in_2,
  input  [1:0] in_3,
  output [1:0] out_4,
  output out_5
);

  wire n1_bit_full_adder_1_out_5;

  _1_bit_full_adder u_1_bit_full_adder_1 (
    .in_1(in_1), .in_2(in_2[0]), .in_3(in_3[0]), .out_4(out_4[0]), .out_5(n1_bit_full_adder_1_out_5));
  _1_bit_full_adder u_1_bit_full_adder_2 (
    .in_1(n1_bit_full_adder_1_out_5), .in_2(in_2[1]), .in_3(in_3[1]), .out_4(out_4[1]), .out_5(out_5));
endmodule

module _18_bit_adder (
  input  [17:0] in_1,
  input  [17:0] in_2,
  output [17:0] out_3,
  output out_4
);

  wire n2_bit_adder_1_out_5, n8_bit_adder_1_out_5;

  _2_bit_adder u_2_bit_adder_1 (
    .in_1(1'b0), .in_2(in_1[1:0]), .in_3(in_2[1:0]), .out_5(n2_bit_adder_1_out_5), .out_4(out_3[1:0]));
  _8_bit_adder u_8_bit_adder_1 (
    .in_2(in_1[9:2]), .in_3(in_2[9:2]), .in_1(n2_bit_adder_1_out_5), .out_5(n8_bit_adder_1_out_5),
    .out_4(out_3[9:2]));
  _8_bit_adder u_8_bit_adder_2 (
    .in_2(in_1[17:10]), .in_3(in_2[17:10]), .in_1(n8_bit_adder_1_out_5), .out_5(out_4), .out_4(out_3[17:10]));
endmodule

module _4_bit_adder (
  input  in_1,
  input  [3:0] in_2,
  input  [3:0] in_3,
  output [3:0] out_4,
  output out_5
);

  wire n2_bit_adder_1_out_5;

  _2_bit_adder u_2_bit_adder_1 (
    .in_1(in_1), .in_2(in_2[1:0]), .in_3(in_3[1:0]), .out_5(n2_bit_adder_1_out_5), .out_4(out_4[1:0]));
  _2_bit_adder u_2_bit_adder_2 (
    .in_1(n2_bit_adder_1_out_5), .in_2(in_2[3:2]), .in_3(in_3[3:2]), .out_5(out_5), .out_4(out_4[3:2]));
endmodule

module _8_bit_adder (
  input  in_1,
  input  [7:0] in_2,
  input  [7:0] in_3,
  output [7:0] out_4,
  output out_5
);

  wire n4_bit_adder_1_out_5;

  _4_bit_adder u_4_bit_adder_1 (
    .in_1(in_1), .in_2(in_2[3:0]), .in_3(in_3[3:0]), .out_5(n4_bit_adder_1_out_5), .out_4(out_4[3:0]));
  _4_bit_adder u_4_bit_adder_2 (
    .in_1(n4_bit_adder_1_out_5), .in_2(in_2[7:4]), .in_3(in_3[7:4]), .out_5(out_5), .out_4(out_4[7:4]));
endmodule

module _16_bit_adder (
  input  in_1,
  input  [15:0] in_2,
  input  [15:0] in_3,
  output [15:0] out_4,
  output out_5
);

  wire n8_bit_adder_1_out_5;

  _8_bit_adder u_8_bit_adder_1 (
    .in_2(in_2[7:0]), .in_3(in_3[7:0]), .in_1(in_1), .out_5(n8_bit_adder_1_out_5), .out_4(out_4[7:0]));
  _8_bit_adder u_8_bit_adder_2 (
    .in_2(in_2[15:8]), .in_3(in_3[15:8]), .in_1(n8_bit_adder_1_out_5), .out_5(out_5), .out_4(out_4[15:8]));
endmodule

module _18_bit_and (
  input  [17:0] in_1,
  input  [17:0] in_2,
  output [17:0] out_3
);

  and and_1 (out_3[0], in_1[0], in_2[0]);
  and and_2 (out_3[1], in_1[1], in_2[1]);
  and and_3 (out_3[2], in_1[2], in_2[2]);
  and and_4 (out_3[3], in_1[3], in_2[3]);
  and and_5 (out_3[4], in_1[4], in_2[4]);
  and and_6 (out_3[5], in_1[5], in_2[5]);
  and and_7 (out_3[6], in_1[6], in_2[6]);
  and and_8 (out_3[7], in_1[7], in_2[7]);
  and and_9 (out_3[8], in_1[8], in_2[8]);
  and and_10 (out_3[9], in_1[9], in_2[9]);
  and and_11 (out_3[10], in_1[10], in_2[10]);
  and and_12 (out_3[11], in_1[11], in_2[11]);
  and and_13 (out_3[12], in_1[12], in_2[12]);
  and and_14 (out_3[13], in_1[13], in_2[13]);
  and and_15 (out_3[14], in_1[14], in_2[14]);
  and and_16 (out_3[15], in_1[15], in_2[15]);
  and and_17 (out_3[16], in_1[16], in_2[16]);
  and and_18 (out_3[17], in_1[17], in_2[17]);
endmodule

module _18_bit_or (
  input  [17:0] in_1,
  input  [17:0] in_2,
  output [17:0] out_3
);

  or or_1 (out_3[0], in_1[0], in_2[0]);
  or or_2 (out_3[1], in_1[1], in_2[1]);
  or or_3 (out_3[2], in_1[2], in_2[2]);
  or or_4 (out_3[3], in_1[3], in_2[3]);
  or or_5 (out_3[4], in_1[4], in_2[4]);
  or or_6 (out_3[5], in_1[5], in_2[5]);
  or or_7 (out_3[6], in_1[6], in_2[6]);
  or or_8 (out_3[7], in_1[7], in_2[7]);
  or or_9 (out_3[8], in_1[8], in_2[8]);
  or or_10 (out_3[9], in_1[9], in_2[9]);
  or or_11 (out_3[10], in_1[10], in_2[10]);
  or or_12 (out_3[11], in_1[11], in_2[11]);
  or or_13 (out_3[12], in_1[12], in_2[12]);
  or or_14 (out_3[13], in_1[13], in_2[13]);
  or or_15 (out_3[14], in_1[14], in_2[14]);
  or or_16 (out_3[15], in_1[15], in_2[15]);
  or or_17 (out_3[16], in_1[16], in_2[16]);
  or or_18 (out_3[17], in_1[17], in_2[17]);
endmodule

module _18_bit_register (
  input  [3:0] read_register_1,
  input  [3:0] write_register,
  input  [3:0] read_register_2,
  input  [17:0] input_data,
  input  regWrite,
  input  Clock,
  input  reset_siignal,
  output [17:0] read_data_1,
  output [17:0] read_data_2
);

  wire and_1_out, and_2_out, and_3_out, and_4_out, and_5_out, and_6_out, and_7_out, and_8_out, and_9_out,
       and_10_out, and_11_out, and_12_out, and_13_out, and_14_out, and_15_out, and_16_out, decoder_1_out0,
       decoder_1_out1, decoder_1_out2, decoder_1_out3, decoder_1_out4, decoder_1_out5, decoder_1_out6,
       decoder_1_out7, decoder_1_out8, decoder_1_out9, decoder_1_out10, decoder_1_out11, decoder_1_out12,
       decoder_1_out13, decoder_1_out14, decoder_1_out15;
  wire [17:0] register_1_q, register_2_q, register_3_q, register_4_q, register_5_q, register_6_q,
       register_7_q, register_8_q, register_9_q, register_10_q, register_11_q, register_12_q, register_13_q,
       register_14_q, register_15_q, register_16_q;

  Decoder #(.select(4)) decoder_1 (
    .out0(decoder_1_out0), .out1(decoder_1_out1), .out2(decoder_1_out2), .out3(decoder_1_out3),
    .out4(decoder_1_out4), .out5(decoder_1_out5), .out6(decoder_1_out6), .out7(decoder_1_out7),
    .out8(decoder_1_out8), .out9(decoder_1_out9), .out10(decoder_1_out10), .out11(decoder_1_out11),
    .out12(decoder_1_out12), .out13(decoder_1_out13), .out14(decoder_1_out14), .out15(decoder_1_out15),
    .sel(write_register));  // open: en
  and and_1 (and_1_out, decoder_1_out0, regWrite);
  and and_2 (and_2_out, decoder_1_out1, regWrite);
  and and_3 (and_3_out, decoder_1_out2, regWrite);
  and and_4 (and_4_out, decoder_1_out3, regWrite);
  and and_5 (and_5_out, decoder_1_out4, regWrite);
  and and_6 (and_6_out, decoder_1_out5, regWrite);
  and and_7 (and_7_out, decoder_1_out6, regWrite);
  and and_8 (and_8_out, decoder_1_out7, regWrite);
  Register #(.width(18)) register_1 (
    .D(input_data), .en(and_1_out), .Q(register_1_q), .clk(Clock), .clr(reset_siignal));
  Register #(.width(18)) register_2 (
    .D(input_data), .en(and_2_out), .Q(register_2_q), .clk(Clock), .clr(reset_siignal));
  Register #(.width(18)) register_3 (
    .D(input_data), .en(and_3_out), .Q(register_3_q), .clk(Clock), .clr(reset_siignal));
  Register #(.width(18)) register_4 (
    .D(input_data), .en(and_4_out), .Q(register_4_q), .clk(Clock), .clr(reset_siignal));
  Register #(.width(18)) register_5 (
    .D(input_data), .en(and_5_out), .Q(register_5_q), .clk(Clock), .clr(reset_siignal));
  Register #(.width(18)) register_6 (
    .D(input_data), .en(and_6_out), .Q(register_6_q), .clk(Clock), .clr(reset_siignal));
  Register #(.width(18)) register_7 (
    .D(input_data), .en(and_7_out), .Q(register_7_q), .clk(Clock), .clr(reset_siignal));
  Register #(.width(18)) register_8 (
    .D(input_data), .en(and_8_out), .Q(register_8_q), .clk(Clock), .clr(reset_siignal));
  and and_9 (and_9_out, decoder_1_out15, regWrite);
  and and_10 (and_10_out, decoder_1_out14, regWrite);
  and and_11 (and_11_out, decoder_1_out13, regWrite);
  and and_12 (and_12_out, decoder_1_out12, regWrite);
  and and_13 (and_13_out, decoder_1_out11, regWrite);
  and and_14 (and_14_out, decoder_1_out10, regWrite);
  and and_15 (and_15_out, decoder_1_out9, regWrite);
  and and_16 (and_16_out, decoder_1_out8, regWrite);
  Register #(.width(18)) register_9 (
    .D(input_data), .en(and_9_out), .Q(register_9_q), .clk(Clock), .clr(reset_siignal));
  Register #(.width(18)) register_10 (
    .D(input_data), .en(and_10_out), .Q(register_10_q), .clk(Clock), .clr(reset_siignal));
  Register #(.width(18)) register_11 (
    .D(input_data), .en(and_11_out), .Q(register_11_q), .clk(Clock), .clr(reset_siignal));
  Register #(.width(18)) register_12 (.D(input_data), .en(and_12_out), .Q(register_12_q), .clk(Clock));  // open: clr
  Register #(.width(18)) register_13 (
    .D(input_data), .en(and_13_out), .Q(register_13_q), .clk(Clock), .clr(reset_siignal));
  Register #(.width(18)) register_14 (
    .D(input_data), .en(and_14_out), .Q(register_14_q), .clk(Clock), .clr(reset_siignal));
  Register #(.width(18)) register_15 (
    .D(input_data), .en(and_15_out), .Q(register_15_q), .clk(Clock), .clr(reset_siignal));
  Register #(.width(18)) register_16 (
    .D(input_data), .en(and_16_out), .Q(register_16_q), .clk(Clock), .clr(reset_siignal));
  Multiplexer #(.select(4), .width(18)) multiplexer_1 (
    .in0(register_1_q), .in1(register_2_q), .in2(register_3_q), .in3(register_4_q), .in4(register_5_q),
    .in5(register_6_q), .in6(register_7_q), .in7(register_8_q), .in8(register_9_q), .in9(register_10_q),
    .in10(register_11_q), .in11(register_12_q), .in12(register_13_q), .in13(register_14_q),
    .in14(register_15_q), .in15(register_16_q), .out(read_data_1), .sel(read_register_1));  // open: en
  Multiplexer #(.select(4), .width(18)) multiplexer_2 (
    .in0(register_1_q), .in1(register_2_q), .in2(register_3_q), .in3(register_4_q), .in4(register_5_q),
    .in5(register_6_q), .in6(register_7_q), .in7(register_8_q), .in8(register_9_q), .in9(register_10_q),
    .in10(register_11_q), .in11(register_12_q), .in12(register_13_q), .in13(register_14_q),
    .in14(register_15_q), .in15(register_16_q), .out(read_data_2), .sel(read_register_2));  // open: en
endmodule

module _18_bit_xor (
  input  [17:0] in_1,
  input  [17:0] in_2,
  output [17:0] out_3
);

  xor xor_1 (out_3[0], in_1[0], in_2[0]);
  xor xor_2 (out_3[1], in_1[1], in_2[1]);
  xor xor_3 (out_3[2], in_1[2], in_2[2]);
  xor xor_4 (out_3[3], in_1[3], in_2[3]);
  xor xor_5 (out_3[4], in_1[4], in_2[4]);
  xor xor_6 (out_3[5], in_1[5], in_2[5]);
  xor xor_7 (out_3[6], in_1[6], in_2[6]);
  xor xor_8 (out_3[7], in_1[7], in_2[7]);
  xor xor_9 (out_3[8], in_1[8], in_2[8]);
  xor xor_10 (out_3[9], in_1[9], in_2[9]);
  xor xor_11 (out_3[10], in_1[10], in_2[10]);
  xor xor_12 (out_3[11], in_1[11], in_2[11]);
  xor xor_13 (out_3[12], in_1[12], in_2[12]);
  xor xor_14 (out_3[13], in_1[13], in_2[13]);
  xor xor_15 (out_3[14], in_1[14], in_2[14]);
  xor xor_16 (out_3[15], in_1[15], in_2[15]);
  xor xor_17 (out_3[16], in_1[16], in_2[16]);
  xor xor_18 (out_3[17], in_1[17], in_2[17]);
endmodule

module ALU (
  input  [17:0] data_1,
  input  [17:0] data_2,
  input  ALU_signal,
  input  in_4,
  input  in_5,
  input  and_signals,
  input  in_7,
  input  or_signals,
  input  in_9,
  input  xor_signals,
  input  in_11,
  output [17:0] alu_result,
  output regWrite_signal,
  output overflow_bit
);

  wire [3:0] or_4_out;
  wire [17:0] n18_bit_adder_1_out_3, n18_bit_and_1_out_3, n18_bit_or_1_out_3, n18_bit_xor_1_out_3;

  _18_bit_adder u_18_bit_adder_1 (.in_1(data_1), .in_2(data_2), .out_4(overflow_bit), .out_3(n18_bit_adder_1_out_3));
  _18_bit_and u_18_bit_and_1 (.in_1(data_1), .in_2(data_2), .out_3(n18_bit_and_1_out_3));
  _18_bit_or u_18_bit_or_1 (.in_1(data_1), .in_2(data_2), .out_3(n18_bit_or_1_out_3));
  _18_bit_xor u_18_bit_xor_1 (.in_1(data_1), .in_2(data_2), .out_3(n18_bit_xor_1_out_3));
  or or_1 (or_4_out[3], in_4, in_5);
  or or_2 (or_4_out[2], and_signals, in_7);
  Multiplexer #(.select(4), .width(18)) multiplexer_1 (
    .in1(n18_bit_xor_1_out_3), .in2(n18_bit_or_1_out_3), .in4(n18_bit_and_1_out_3),
    .in8(n18_bit_adder_1_out_3), .out(alu_result), .sel(or_4_out), .en(ALU_signal));  // open: in0, in3, in5, in6, in7, in9, in10, in11, in12, in13, in14, in15
  or or_3 (or_4_out[1], or_signals, in_9);
  or or_4 (or_4_out[0], xor_signals, in_11);

  assign regWrite_signal = ALU_signal;

  // Notes on the sheet:
  //   Add
  //   And
  //   Or
  //   Xor
  //   add signals
endmodule

module CPU (
  input  [17:0] assembly_code,
  output add,
  output \and ,
  output \or ,
  output \xor ,
  output imm_add,
  output imm_and,
  output imm_or,
  output imm_xor,
  output jump,
  output load,
  output store,
  output beq,
  output blt,
  output bgt,
  output ble,
  output bge,
  output jump_offset_signal,
  output branch_offset_signal,
  output [13:0] process_data,
  output defaullt_offset_signal,
  output imm_signal,
  output alu_signal
);

  Decoder #(.select(4)) decoder_1 (
    .out0(add), .out1(\and ), .out2(\or ), .out3(\xor ), .out4(imm_add), .out5(imm_and), .out6(imm_or),
    .out7(imm_xor), .out8(jump), .out9(load), .out10(store), .out11(beq), .out12(blt), .out13(bgt),
    .out14(ble), .out15(bge), .sel(assembly_code[17:14]));  // open: en
  or or_1 (imm_signal, imm_xor, imm_or, imm_and, imm_add);
  or or_2 (alu_signal, imm_xor, imm_or, imm_and, imm_add, \xor , \or , \and , add);
  or or_3 (branch_offset_signal, beq, blt, bgt, ble, bge);
  or or_4 (defaullt_offset_signal, add, \and , \or , \xor , imm_add, imm_and, imm_or, imm_xor, load, store);

  assign jump_offset_signal = jump;
  assign process_data = assembly_code[13:0];

  // Notes on the sheet:
  //   opcode
endmodule

module PC (
  input  reset_signal,
  input  clock,
  input  [9:0] branch_offset,
  input  [9:0] jump_offset,
  input  [1:0] address_signal,
  output [9:0] current_address,
  output address_overflow
);

  wire n2_bit_adder_1_out_5;
  wire [1:0] register_3_q;
  wire [9:0] address_register_q, multiplexer_1_out, multiplexer_2_out, register_1_q, register_2_q;

  Register #(.width(10), .trigger("falling")) register_1 (
    .D(branch_offset), .Q(register_1_q), .clk(clock));  // open: en, clr
  Register #(.width(10), .trigger("falling")) register_2 (
    .D(jump_offset), .Q(register_2_q), .clk(clock));  // open: en, clr
  Register #(.width(2), .trigger("falling")) register_3 (
    .D(address_signal), .Q(register_3_q), .clk(clock));  // open: en, clr
  Register #(.width(10), .trigger("falling")) address_register (
    .D(current_address), .en(1'b1), .Q(address_register_q), .clk(clock), .clr(reset_signal));
  // Probe on register_3_q
  // Probe on address_register_q
  Multiplexer #(.select(2), .width(10)) multiplexer_1 (
    .in0(multiplexer_2_out), .in1(register_1_q), .in2(register_2_q), .out(multiplexer_1_out),
    .sel(register_3_q));  // open: in3, en
  // Probe on multiplexer_1_out
  D_Flip_Flop d_ff_1 ();  // open: clk, D, Q, Qn, preset, en, reset
  _2_bit_adder u_2_bit_adder_1 (
    .in_1(1'b0), .in_2(address_register_q[1:0]), .in_3(multiplexer_1_out[1:0]), .out_5(n2_bit_adder_1_out_5),
    .out_4(current_address[1:0]));
  Multiplexer #(.width(10)) multiplexer_2 (
    .in0(10'h1), .in1({10{1'b0}}), .out(multiplexer_2_out), .sel(reset_signal));  // open: en
  _8_bit_adder u_8_bit_adder_1 (
    .in_2(address_register_q[9:2]), .in_3(multiplexer_1_out[9:2]), .in_1(n2_bit_adder_1_out_5),
    .out_5(address_overflow), .out_4(current_address[9:2]));

  // Notes on the sheet:
  //   0: default
  //   1: branch
  //   2: jump
endmodule

module _1_bit_half_sub (
  input  in_1,
  input  in_2,
  output difference,
  output borrow_out
);

  wire not_1_out;

  not not_1 (not_1_out, in_1);
  xor xor_1 (difference, in_1, in_2);
  and and_1 (borrow_out, in_2, not_1_out);
endmodule

module _1_bit_full__sub (
  input  borrow_in,
  input  in_2,
  input  in_3,
  output difference,
  output borrow_out
);

  wire n1_bit_half_sub_1_borrow_out, n1_bit_half_sub_1_difference, n1_bit_half_sub_2_borrow_out;

  _1_bit_half_sub u_1_bit_half_sub_1 (
    .in_1(in_2), .in_2(in_3), .difference(n1_bit_half_sub_1_difference),
    .borrow_out(n1_bit_half_sub_1_borrow_out));
  _1_bit_half_sub u_1_bit_half_sub_2 (
    .in_1(n1_bit_half_sub_1_difference), .in_2(borrow_in), .difference(difference),
    .borrow_out(n1_bit_half_sub_2_borrow_out));
  or or_1 (borrow_out, n1_bit_half_sub_1_borrow_out, n1_bit_half_sub_2_borrow_out);
endmodule

module _2_bit_sub (
  input  in_1,
  input  [1:0] in_2,
  input  [1:0] in_3,
  output [1:0] out_4,
  output out_5
);

  wire n1_bit_full__sub_1_borrow_out;

  _1_bit_full__sub u_1_bit_full__sub_1 (
    .borrow_in(in_1), .in_2(in_2[0]), .in_3(in_3[0]), .difference(out_4[0]),
    .borrow_out(n1_bit_full__sub_1_borrow_out));
  _1_bit_full__sub u_1_bit_full__sub_2 (
    .borrow_in(n1_bit_full__sub_1_borrow_out), .in_2(in_2[1]), .in_3(in_3[1]), .difference(out_4[1]),
    .borrow_out(out_5));
endmodule

module _4_bit_sub (
  input  in_1,
  input  [3:0] in_2,
  input  [3:0] in_3,
  output [3:0] out_4,
  output out_5
);

  wire n2_bit_sub_1_out_5;

  _2_bit_sub u_2_bit_sub_1 (
    .in_1(in_1), .in_2(in_2[1:0]), .in_3(in_3[1:0]), .out_5(n2_bit_sub_1_out_5), .out_4(out_4[1:0]));
  _2_bit_sub u_2_bit_sub_2 (
    .in_1(n2_bit_sub_1_out_5), .in_2(in_2[3:2]), .in_3(in_3[3:2]), .out_5(out_5), .out_4(out_4[3:2]));
endmodule

module _8_bit_sub (
  input  in_1,
  input  [7:0] in_2,
  input  [7:0] in_3,
  output [7:0] out_4,
  output out_5
);

  wire n4_bit_sub_1_out_5;

  _4_bit_sub u_4_bit_sub_1 (
    .in_1(in_1), .in_2(in_2[3:0]), .in_3(in_3[3:0]), .out_5(n4_bit_sub_1_out_5), .out_4(out_4[3:0]));
  _4_bit_sub u_4_bit_sub_2 (
    .in_1(n4_bit_sub_1_out_5), .in_2(in_2[7:4]), .in_3(in_3[7:4]), .out_5(out_5), .out_4(out_4[7:4]));
endmodule

module _18_bit_sub (
  input  [17:0] in_1,
  input  [17:0] in_2,
  output [17:0] out_3,
  output out_4
);

  wire n2_bit_sub_1_out_5, n8_bit_sub_1_out_5;

  _2_bit_sub u_2_bit_sub_1 (
    .in_1(1'b0), .in_2(in_1[1:0]), .in_3(in_2[1:0]), .out_5(n2_bit_sub_1_out_5), .out_4(out_3[1:0]));
  _8_bit_sub u_8_bit_sub_1 (
    .in_1(n2_bit_sub_1_out_5), .in_2(in_1[9:2]), .in_3(in_2[9:2]), .out_5(n8_bit_sub_1_out_5),
    .out_4(out_3[9:2]));
  _8_bit_sub u_8_bit_sub_2 (
    .in_1(n8_bit_sub_1_out_5), .in_2(in_1[17:10]), .in_3(in_2[17:10]), .out_5(out_4), .out_4(out_3[17:10]));
endmodule

module _10_bit_sub (
  input  [9:0] in_1,
  input  [9:0] in_2,
  output [9:0] out_3,
  output out_4
);

  wire n2_bit_sub_1_out_5, n4_bit_sub_1_out_5;

  _2_bit_sub u_2_bit_sub_1 (
    .in_1(1'b0), .in_2(in_1[1:0]), .in_3(in_2[1:0]), .out_5(n2_bit_sub_1_out_5), .out_4(out_3[1:0]));
  _4_bit_sub u_4_bit_sub_1 (
    .in_1(n2_bit_sub_1_out_5), .in_2(in_1[5:2]), .in_3(in_2[5:2]), .out_5(n4_bit_sub_1_out_5),
    .out_4(out_3[5:2]));
  _4_bit_sub u_4_bit_sub_2 (
    .in_1(n4_bit_sub_1_out_5), .in_2(in_1[9:6]), .in_3(in_2[9:6]), .out_5(out_4), .out_4(out_3[9:6]));
endmodule

module _6_18_bit_extender (
  input  [5:0] \input ,
  output [17:0] out_2
);


  assign out_2 = {{13{\input [5]}}, \input [4:0]};
endmodule

module _1_bit_comparator (
  input  A,
  input  B,
  input  IAgtB,
  input  IAeqB,
  input  IAltB,
  output OAgtB,
  output OAeqB,
  output OAltB
);

  wire and_1_out, and_2_out, not_1_out, not_2_out, xnor_1_out;

  not not_1 (not_1_out, A);
  not not_2 (not_2_out, B);
  and and_1 (and_1_out, not_2_out, IAeqB, A);
  and and_2 (and_2_out, B, IAeqB, not_1_out);
  or or_1 (OAgtB, IAgtB, and_1_out);
  xnor xnor_1 (xnor_1_out, A, B);
  and and_3 (OAeqB, xnor_1_out, IAeqB);
  or or_2 (OAltB, and_2_out, IAltB);
endmodule

module _18_bit_comparator (
  input  [17:0] InputA,
  input  [17:0] InputB,
  output OutputAgtB,
  output OutputAeqtB,
  output OutputAltB
);

  wire n1_bit_comparator_1_oaeqb, n1_bit_comparator_1_oagtb, n1_bit_comparator_1_oaltb,
       n1_bit_comparator_2_oaeqb, n1_bit_comparator_2_oagtb, n1_bit_comparator_2_oaltb,
       n1_bit_comparator_3_oaeqb, n1_bit_comparator_3_oagtb, n1_bit_comparator_3_oaltb,
       n1_bit_comparator_4_oaeqb, n1_bit_comparator_4_oagtb, n1_bit_comparator_4_oaltb,
       n1_bit_comparator_5_oaeqb, n1_bit_comparator_5_oagtb, n1_bit_comparator_5_oaltb,
       n1_bit_comparator_6_oaeqb, n1_bit_comparator_6_oagtb, n1_bit_comparator_6_oaltb,
       n1_bit_comparator_7_oaeqb, n1_bit_comparator_7_oagtb, n1_bit_comparator_7_oaltb,
       n1_bit_comparator_8_oaeqb, n1_bit_comparator_8_oagtb, n1_bit_comparator_8_oaltb,
       n1_bit_comparator_9_oaeqb, n1_bit_comparator_9_oagtb, n1_bit_comparator_9_oaltb,
       n1_bit_comparator_10_oaeqb, n1_bit_comparator_10_oagtb, n1_bit_comparator_10_oaltb,
       n1_bit_comparator_11_oaeqb, n1_bit_comparator_11_oagtb, n1_bit_comparator_11_oaltb,
       n1_bit_comparator_12_oaeqb, n1_bit_comparator_12_oagtb, n1_bit_comparator_12_oaltb,
       n1_bit_comparator_13_oaeqb, n1_bit_comparator_13_oagtb, n1_bit_comparator_13_oaltb,
       n1_bit_comparator_14_oaeqb, n1_bit_comparator_14_oagtb, n1_bit_comparator_14_oaltb,
       n1_bit_comparator_15_oaeqb, n1_bit_comparator_15_oagtb, n1_bit_comparator_15_oaltb,
       n1_bit_comparator_16_oaeqb, n1_bit_comparator_16_oagtb, n1_bit_comparator_16_oaltb,
       n1_bit_comparator_17_oaeqb, n1_bit_comparator_17_oagtb, n1_bit_comparator_17_oaltb,
       n1_bit_comparator_18_oagtb, n1_bit_comparator_18_oaltb, not_1_out, not_2_out, xor_1_out;

  _1_bit_comparator u_1_bit_comparator_1 (
    .IAgtB(1'b0), .IAeqB(1'b1), .IAltB(1'b0), .OAgtB(n1_bit_comparator_1_oagtb),
    .OAeqB(n1_bit_comparator_1_oaeqb), .OAltB(n1_bit_comparator_1_oaltb), .A(InputA[17]), .B(InputB[17]));
  _1_bit_comparator u_1_bit_comparator_2 (
    .IAgtB(n1_bit_comparator_1_oagtb), .IAeqB(n1_bit_comparator_1_oaeqb), .IAltB(n1_bit_comparator_1_oaltb),
    .OAgtB(n1_bit_comparator_2_oagtb), .OAeqB(n1_bit_comparator_2_oaeqb), .OAltB(n1_bit_comparator_2_oaltb),
    .A(InputA[16]), .B(InputB[16]));
  _1_bit_comparator u_1_bit_comparator_3 (
    .IAgtB(n1_bit_comparator_2_oagtb), .IAeqB(n1_bit_comparator_2_oaeqb), .IAltB(n1_bit_comparator_2_oaltb),
    .OAgtB(n1_bit_comparator_3_oagtb), .OAeqB(n1_bit_comparator_3_oaeqb), .OAltB(n1_bit_comparator_3_oaltb),
    .A(InputA[15]), .B(InputB[15]));
  _1_bit_comparator u_1_bit_comparator_4 (
    .IAgtB(n1_bit_comparator_3_oagtb), .IAeqB(n1_bit_comparator_3_oaeqb), .IAltB(n1_bit_comparator_3_oaltb),
    .OAgtB(n1_bit_comparator_4_oagtb), .OAeqB(n1_bit_comparator_4_oaeqb), .OAltB(n1_bit_comparator_4_oaltb),
    .A(InputA[14]), .B(InputB[14]));
  _1_bit_comparator u_1_bit_comparator_5 (
    .IAgtB(n1_bit_comparator_4_oagtb), .IAeqB(n1_bit_comparator_4_oaeqb), .IAltB(n1_bit_comparator_4_oaltb),
    .OAgtB(n1_bit_comparator_5_oagtb), .OAeqB(n1_bit_comparator_5_oaeqb), .OAltB(n1_bit_comparator_5_oaltb),
    .A(InputA[13]), .B(InputB[13]));
  _1_bit_comparator u_1_bit_comparator_6 (
    .IAgtB(n1_bit_comparator_5_oagtb), .IAeqB(n1_bit_comparator_5_oaeqb), .IAltB(n1_bit_comparator_5_oaltb),
    .OAgtB(n1_bit_comparator_6_oagtb), .OAeqB(n1_bit_comparator_6_oaeqb), .OAltB(n1_bit_comparator_6_oaltb),
    .A(InputA[12]), .B(InputB[12]));
  _1_bit_comparator u_1_bit_comparator_7 (
    .IAgtB(n1_bit_comparator_8_oagtb), .IAeqB(n1_bit_comparator_8_oaeqb), .IAltB(n1_bit_comparator_8_oaltb),
    .OAgtB(n1_bit_comparator_7_oagtb), .OAeqB(n1_bit_comparator_7_oaeqb), .OAltB(n1_bit_comparator_7_oaltb),
    .A(InputA[10]), .B(InputB[10]));
  _1_bit_comparator u_1_bit_comparator_8 (
    .IAgtB(n1_bit_comparator_6_oagtb), .IAeqB(n1_bit_comparator_6_oaeqb), .IAltB(n1_bit_comparator_6_oaltb),
    .OAgtB(n1_bit_comparator_8_oagtb), .OAeqB(n1_bit_comparator_8_oaeqb), .OAltB(n1_bit_comparator_8_oaltb),
    .A(InputA[11]), .B(InputB[11]));
  _1_bit_comparator u_1_bit_comparator_9 (
    .IAgtB(n1_bit_comparator_7_oagtb), .IAeqB(n1_bit_comparator_7_oaeqb), .IAltB(n1_bit_comparator_7_oaltb),
    .OAgtB(n1_bit_comparator_9_oagtb), .OAeqB(n1_bit_comparator_9_oaeqb), .OAltB(n1_bit_comparator_9_oaltb),
    .A(InputA[9]), .B(InputB[9]));
  _1_bit_comparator u_1_bit_comparator_10 (
    .IAgtB(n1_bit_comparator_9_oagtb), .IAeqB(n1_bit_comparator_9_oaeqb), .IAltB(n1_bit_comparator_9_oaltb),
    .OAgtB(n1_bit_comparator_10_oagtb), .OAeqB(n1_bit_comparator_10_oaeqb),
    .OAltB(n1_bit_comparator_10_oaltb), .A(InputA[8]), .B(InputB[8]));
  _1_bit_comparator u_1_bit_comparator_11 (
    .IAgtB(n1_bit_comparator_10_oagtb), .IAeqB(n1_bit_comparator_10_oaeqb),
    .IAltB(n1_bit_comparator_10_oaltb), .OAgtB(n1_bit_comparator_11_oagtb),
    .OAeqB(n1_bit_comparator_11_oaeqb), .OAltB(n1_bit_comparator_11_oaltb), .A(InputA[7]), .B(InputB[7]));
  _1_bit_comparator u_1_bit_comparator_12 (
    .IAgtB(n1_bit_comparator_11_oagtb), .IAeqB(n1_bit_comparator_11_oaeqb),
    .IAltB(n1_bit_comparator_11_oaltb), .OAgtB(n1_bit_comparator_12_oagtb),
    .OAeqB(n1_bit_comparator_12_oaeqb), .OAltB(n1_bit_comparator_12_oaltb), .A(InputA[6]), .B(InputB[6]));
  _1_bit_comparator u_1_bit_comparator_13 (
    .IAgtB(n1_bit_comparator_12_oagtb), .IAeqB(n1_bit_comparator_12_oaeqb),
    .IAltB(n1_bit_comparator_12_oaltb), .OAgtB(n1_bit_comparator_13_oagtb),
    .OAeqB(n1_bit_comparator_13_oaeqb), .OAltB(n1_bit_comparator_13_oaltb), .A(InputA[5]), .B(InputB[5]));
  _1_bit_comparator u_1_bit_comparator_14 (
    .IAgtB(n1_bit_comparator_13_oagtb), .IAeqB(n1_bit_comparator_13_oaeqb),
    .IAltB(n1_bit_comparator_13_oaltb), .OAgtB(n1_bit_comparator_14_oagtb),
    .OAeqB(n1_bit_comparator_14_oaeqb), .OAltB(n1_bit_comparator_14_oaltb), .A(InputA[4]), .B(InputB[4]));
  _1_bit_comparator u_1_bit_comparator_15 (
    .IAgtB(n1_bit_comparator_14_oagtb), .IAeqB(n1_bit_comparator_14_oaeqb),
    .IAltB(n1_bit_comparator_14_oaltb), .OAgtB(n1_bit_comparator_15_oagtb),
    .OAeqB(n1_bit_comparator_15_oaeqb), .OAltB(n1_bit_comparator_15_oaltb), .A(InputA[3]), .B(InputB[3]));
  _1_bit_comparator u_1_bit_comparator_16 (
    .IAgtB(n1_bit_comparator_15_oagtb), .IAeqB(n1_bit_comparator_15_oaeqb),
    .IAltB(n1_bit_comparator_15_oaltb), .OAgtB(n1_bit_comparator_16_oagtb),
    .OAeqB(n1_bit_comparator_16_oaeqb), .OAltB(n1_bit_comparator_16_oaltb), .A(InputA[2]), .B(InputB[2]));
  _1_bit_comparator u_1_bit_comparator_17 (
    .IAgtB(n1_bit_comparator_16_oagtb), .IAeqB(n1_bit_comparator_16_oaeqb),
    .IAltB(n1_bit_comparator_16_oaltb), .OAgtB(n1_bit_comparator_17_oagtb),
    .OAeqB(n1_bit_comparator_17_oaeqb), .OAltB(n1_bit_comparator_17_oaltb), .A(InputA[1]), .B(InputB[1]));
  _1_bit_comparator u_1_bit_comparator_18 (
    .IAgtB(n1_bit_comparator_17_oagtb), .IAeqB(n1_bit_comparator_17_oaeqb),
    .IAltB(n1_bit_comparator_17_oaltb), .OAgtB(n1_bit_comparator_18_oagtb), .OAeqB(OutputAeqtB),
    .OAltB(n1_bit_comparator_18_oaltb), .A(InputA[0]), .B(InputB[0]));
  xor xor_1 (xor_1_out, InputB[17], InputA[17]);
  not not_1 (not_1_out, n1_bit_comparator_18_oagtb);
  not not_2 (not_2_out, n1_bit_comparator_18_oaltb);
  Multiplexer multiplexer_1 (
    .in0(n1_bit_comparator_18_oagtb), .in1(not_1_out), .out(OutputAgtB), .sel(xor_1_out));  // open: en
  Multiplexer multiplexer_2 (
    .in0(n1_bit_comparator_18_oaltb), .in1(not_2_out), .out(OutputAltB), .sel(xor_1_out));  // open: en
endmodule

module ALU_separator (
  input  [13:0] _14_bit_input,
  output [17:0] _18_bit_output,
  output [3:0] Source_2,
  output [3:0] Source_1,
  output [3:0] Dest
);

  _6_18_bit_extender u_6_18_bit_extender_1 (.\input (_14_bit_input[5:0]), .out_2(_18_bit_output));

  assign Dest = _14_bit_input[13:10];
  assign Source_1 = _14_bit_input[9:6];
  assign Source_2 = _14_bit_input[5:2];
endmodule

module offset_selector (
  input  jump,
  input  branch,
  input  \default ,
  output [1:0] offset_selector
);

  Multiplexer #(.select(3), .width(2)) multiplexer_1 (
    .in0(2'b00), .in1(2'b10), .in2(2'b01), .in4(2'b00), .out(offset_selector), .sel({\default , branch, jump}));  // open: in3, in5, in6, in7, en

  // Notes on the sheet:
  //   100: default
  //   010: branch
  //   001: jump
endmodule

module jump_parser (
  input  [13:0] input_data,
  input  jump_signal,
  output [9:0] jump_offset
);

  Multiplexer #(.width(10)) multiplexer_1 (
    .in0({10{1'b0}}), .in1(input_data[13:4]), .out(jump_offset), .sel(jump_signal));  // open: en
endmodule

module address_stabiliser (
  input  [9:0] current_address,
  input  [9:0] offset,
  output [9:0] output_address,
  output overflow
);

  wire [9:0] n10_bit_adder_1_out_3;

  _10_bit_adder u_10_bit_adder_1 (
    .in_1(current_address), .in_2(offset), .out_4(overflow), .out_3(n10_bit_adder_1_out_3));
  Multiplexer #(.width(10)) multiplexer_1 (
    .in0(offset), .in1(10'h1), .out(output_address), .sel(n10_bit_adder_1_out_3[9]));  // open: en
endmodule

module _10_bit_adder (
  input  [9:0] in_1,
  input  [9:0] in_2,
  output [9:0] out_3,
  output out_4
);

  wire n2_bit_adder_1_out_5, n4_bit_adder_1_out_5;

  _2_bit_adder u_2_bit_adder_1 (
    .in_1(1'b0), .in_2(in_1[1:0]), .in_3(in_2[1:0]), .out_5(n2_bit_adder_1_out_5), .out_4(out_3[1:0]));
  _4_bit_adder u_4_bit_adder_1 (
    .in_1(n2_bit_adder_1_out_5), .in_2(in_1[5:2]), .in_3(in_2[5:2]), .out_5(n4_bit_adder_1_out_5),
    .out_4(out_3[5:2]));
  _4_bit_adder u_4_bit_adder_2 (
    .in_1(n4_bit_adder_1_out_5), .in_2(in_1[9:6]), .in_3(in_2[9:6]), .out_5(out_4), .out_4(out_3[9:6]));
endmodule

module _2_bit_incrementer (
  input  in_1,
  output out_2,
  output out_3
);

  _1_bit_half_adder u_1_bit_half_adder_1 (.in_1(in_1), .in_2(1'b1), .out_3(out_2), .out_4(out_3));
endmodule

module ram_separator (
  input  [13:0] process_data,
  output [3:0] load_register,
  output [9:0] memory_address
);


  assign load_register = process_data[13:10];
  assign memory_address = process_data[9:0];
endmodule

module branch_separator (
  input  [13:0] process_data,
  input  branch_signal,
  output [3:0] read_register_1,
  output [3:0] read_register_2,
  output [5:0] branch_address
);

  Multiplexer #(.width(4)) multiplexer_1 (
    .in0(4'b0000), .in1(process_data[13:10]), .out(read_register_1), .sel(branch_signal));  // open: en
  Multiplexer #(.width(4)) multiplexer_2 (
    .in0(4'b0000), .in1(process_data[9:6]), .out(read_register_2), .sel(branch_signal));  // open: en
  Multiplexer #(.width(6)) multiplexer_3 (
    .in0({6{1'b0}}), .in1(process_data[5:0]), .out(branch_address), .sel(branch_signal));  // open: en
endmodule

module branch_stabiliser (
  input  [17:0] register_1,
  input  [17:0] register_2,
  input  [9:0] current_pc_address,
  input  beq,
  input  blt,
  input  bgt,
  input  ble,
  input  bge,
  input  [5:0] offset,
  output [9:0] branch_offset,
  output overflow
);

  wire multiplexer_1_out, n18_bit_comparator_1_outputaeqtb, n18_bit_comparator_1_outputagtb,
       n18_bit_comparator_1_outputaltb, or_1_out, or_2_out;
  wire [9:0] address_stabiliser_1_output_address, n6_10_bit_extender_1_out_2;

  _18_bit_comparator u_18_bit_comparator_1 (
    .InputA(register_1), .InputB(register_2), .OutputAgtB(n18_bit_comparator_1_outputagtb),
    .OutputAeqtB(n18_bit_comparator_1_outputaeqtb), .OutputAltB(n18_bit_comparator_1_outputaltb));
  or or_1 (or_1_out, n18_bit_comparator_1_outputaeqtb, n18_bit_comparator_1_outputagtb);
  or or_2 (or_2_out, n18_bit_comparator_1_outputaeqtb, n18_bit_comparator_1_outputaltb);
  Multiplexer #(.select(5)) multiplexer_1 (
    .in0(1'b0), .in1(or_1_out), .in2(or_2_out), .in4(n18_bit_comparator_1_outputagtb),
    .in8(n18_bit_comparator_1_outputaltb), .in16(n18_bit_comparator_1_outputaeqtb), .out(multiplexer_1_out),
    .sel({beq, blt, bgt, ble, bge}));  // open: in3, in5, in6, in7, in9, in10, in11, in12, in13, in14, in15, in17, in18, in19, in20, in21, in22, in23, in24, in25, in26, in27, in28, in29, in30, in31, en
  _6_10_bit_extender u_6_10_bit_extender_1 (.\input (offset), .out_2(n6_10_bit_extender_1_out_2));
  address_stabiliser address_stabiliser_1 (
    .output_address(address_stabiliser_1_output_address), .current_address(current_pc_address),
    .offset(n6_10_bit_extender_1_out_2), .overflow(overflow));
  Multiplexer #(.width(10)) multiplexer_2 (
    .in0(10'h1), .in1(address_stabiliser_1_output_address), .out(branch_offset), .sel(multiplexer_1_out));  // open: en

  // Notes on the sheet:
  //   10000: eq
  //   01000: lt
  //   00100: gt
  //   00010: le
  //   00001: ge
endmodule

module _6_10_bit_extender (
  input  [5:0] \input ,
  output [9:0] out_2
);


  assign out_2 = {{5{\input [5]}}, \input [4:0]};
endmodule
